# Fritzing sketch led_cube_sch (saved by Fritzing 0.9.2b)
breadboards: 1

parts:
  Part1 = Arduino Uno (Rev3)
  LED1 = LED - 5mm [color="Green (555nm)" package="5 mm [THT]"]
  LED2 = LED - 5mm [color="Green (555nm)" package="5 mm [THT]"]
  LED3 = LED - 5mm [color="Green (555nm)" package="5 mm [THT]"]
  LED4 = LED - 5mm [color="Green (555nm)" package="5 mm [THT]"]
  LED5 = LED - 5mm [color="Green (555nm)" package="5 mm [THT]"]
  LED6 = LED - 5mm [color="Green (555nm)" package="5 mm [THT]"]
  LED7 = LED - 5mm [color="Green (555nm)" package="5 mm [THT]"]
  LED8 = LED - 5mm [color="Green (555nm)" package="5 mm [THT]"]
  R1 = Resistor [tolerance=±5% resistance=680 package=THT]
  R2 = Resistor [tolerance=±5% resistance=680 package=THT]
  R3 = Resistor [tolerance=±5% resistance=680 package=THT]
  R4 = Resistor [tolerance=±5% resistance=680 package=THT]

nets:
  N1: Part1.D11_PWM/MOSI, LED5.cathode, LED6.cathode, LED7.cathode, LED8.cathode
  N2: Part1.D12/MISO, LED1.cathode, LED2.cathode, LED3.cathode, LED4.cathode
  N3: Part1.D2, R2.Pin_1
  N4: Part1.D3_PWM, R3.Pin_0
  N5: Part1.D4, R4.Pin_1
  N6: Part1.D5_PWM, R1.Pin_0
  N7: LED1.anode, LED6.anode, R1.Pin_1
  N8: LED2.anode, LED5.anode, R4.Pin_0
  N9: LED3.anode, LED8.anode, R3.Pin_1
  N10: LED4.anode, LED7.anode, R2.Pin_0
